# Fritzing sketch raspberry_ir_receive (saved by Fritzing 0.9.3b)
breadboards: 1

parts:
  Raspberry_Pi_1 = Raspberry Pi 3 [part_number=RPI-3-V1.2]
  IR1 = TSOP312.., 314.. [package=THT]

nets:
  N1: Raspberry_Pi_1.GPIO18, IR1.GND
  N2: Raspberry_Pi_1.GND, IR1.Vs
  N3: Raspberry_Pi_1.5V, IR1.Data
